# Fritzing sketch ds1302 (saved by Fritzing 0.9.3b)
breadboards: 1

parts:
  LCD1 = LCD screen
  R1 = Rotary Potentiometer (Small) [maximum_resistance=100kΩ package=THT]
  Part1 = Arduino Uno (Rev3)
  R2 = Resistor [tolerance=±5% resistance=220 package=THT]
  U1 = 实时时钟模块DS1302
  DHT1 = DHT11 Humitidy and Temperature Sensor
  J1 = Piezo Speaker

nets:
  GND: LCD1.VSS, LCD1.R/W, LCD1.LED-, R1.leg2, Part1.GND, U1.GND, DHT1.GND, J1.pin1
  VDD: LCD1.VDD, R1.leg1, Part1.5V, R2.Pin_0, U1.VCC, DHT1.VDD
  N1: LCD1.V0, R1.wiper
  N2: LCD1.RS, Part1.D12/MISO
  N3: LCD1.E, Part1.D11_PWM/MOSI
  N4: LCD1.DB4, Part1.D6_PWM
  N5: LCD1.DB5, Part1.D7
  N6: LCD1.DB6, Part1.D8
  N7: LCD1.DB7, Part1.D9_PWM
  N8: LCD1.LED+, R2.Pin_1
  N9: Part1.D10_PWM/SS, DHT1.DATA
  N10: Part1.D2, U1.RST
  N11: Part1.D3_PWM, U1.DAT
  N12: Part1.D4, U1.CLK
  N13: Part1.D5_PWM, J1.pin2

custom parts:
  DHT11 Humitidy and Temperature Sensor: DHT11 Humidity and Temperature Sensor
